# Fritzing sketch esp32_motor_control (saved by Fritzing 0.9.6b)
circuit board: 9.71478cm x 6.86915cm
breadboards: 1

parts:
  U1 = ESP32-38PinWide [part_number=ESP32-38PinWide]
  J4 = male pin header, 8 pins [form="♂ (male)"]
  J5 = male pin header, 6 pins [form="♂ (male)"]
  J13 = male pin header, 19 pins [form="♂ (male)"]
  A_B_GND_5V = male pin header, 4 pins [form="♂ (male)"]
  A_B_GND_5V_2 = male pin header, 4 pins [form="♂ (male)"]
  A_B_GND_5V_3 = male pin header, 4 pins [form="♂ (male)"]
  A_B_GND_5V_4 = male pin header, 4 pins [form="♂ (male)"]
  J11 = male pin header, 19 pins [form="♂ (male)"]
  GND = Header 2 [package=screwterminal-3.5mm-2_lock]
  J12 = male pin header, 4 pins [form="♂ (male)"]
  gnd_pwm_dir = male pin header, 3 pins [form="♂ (male)"]
  gnd_pwm_dir_2 = male pin header, 3 pins [form="♂ (male)"]
  gnd_pwm_dir_3 = male pin header, 3 pins [form="♂ (male)"]
  gnd_pwm_dir_4 = male pin header, 3 pins [form="♂ (male)"]
  GND_2 = male pin header, 3 pins [form="♂ (male)"]
  5V = male pin header, 3 pins [form="♂ (male)"]

nets:
  N1: U1.3.3, J11.pin19
  N2: U1.GPIO34, J11.pin15
  N3: U1.GPIO35, A_B_GND_5V_4.pin4, J11.pin14
  N4: U1.GPIO32, A_B_GND_5V_4.pin3, J11.pin13
  N5: U1.GPIO33, A_B_GND_5V_3.pin4, J11.pin12
  N6: U1.GPIO25, A_B_GND_5V_3.pin3, J11.pin11
  N7: U1.GPIO26, J11.pin10, gnd_pwm_dir_3.pin2
  N8: U1.GPIO27, A_B_GND_5V_2.pin3, J11.pin9
  N9: U1.GPIO14, J11.pin8, gnd_pwm_dir_3.pin1
  N10: U1.GPIO12, J11.pin7, gnd_pwm_dir_2.pin1
  N11: U1.GND, J13.pin13, J13.pin19, J11.pin6
  N12: U1.GPIO13, J11.pin5, gnd_pwm_dir_2.pin2
  N13: U1.GPIO9, J11.pin4
  N14: U1.GPIO10, J11.pin3
  N15: U1.GPIO11, J11.pin2
  N16: U1.VIN, J11.pin1
  N17: U1.GPIO6, J13.pin1
  N18: U1.GPIO7, J13.pin2
  N19: U1.GPIO8, J13.pin3
  N20: U1.GPIO15, J13.pin4
  N21: U1.GPIO2, J13.pin5
  N22: U1.GPIO0, J13.pin6
  N23: U1.GPIO4, J13.pin7, A_B_GND_5V_2.pin4
  N24: U1.GPIO16, J13.pin8, gnd_pwm_dir_4.pin2
  N25: U1.GPIO17, J13.pin9, gnd_pwm_dir.pin2
  N26: U1.GPIO5, J13.pin10, gnd_pwm_dir_4.pin1
  N27: U1.GPIO18, J13.pin11, A_B_GND_5V.pin3
  N28: U1.GPIO19, J13.pin12, gnd_pwm_dir.pin1
  N29: U1.GPIO21, J13.pin14, J12.pin1
  N30: U1.GPIO3, J13.pin15
  N31: U1.GPIO1, J13.pin16
  N32: U1.GPIO22, J13.pin17, J12.pin2
  N33: U1.GPIO23, J13.pin18, A_B_GND_5V.pin4
  N34: J4.pin1, J4.pin2, J4.pin3, J4.pin4, J4.pin5, J4.pin6, J4.pin7, J4.pin8, A_B_GND_5V.pin2, A_B_GND_5V_2.pin2, A_B_GND_5V_3.pin2, A_B_GND_5V_4.pin2, GND.1, J12.pin4, gnd_pwm_dir.pin3, gnd_pwm_dir_2.pin3, gnd_pwm_dir_3.pin3, gnd_pwm_dir_4.pin3, GND_2.pin1, GND_2.pin2, GND_2.pin3
  N35: J5.pin1, J5.pin2, J5.pin3, J5.pin4, J5.pin5, J5.pin6, A_B_GND_5V.pin1, A_B_GND_5V_2.pin1, A_B_GND_5V_3.pin1, A_B_GND_5V_4.pin1, GND.2, J12.pin3, 5V.pin1, 5V.pin2, 5V.pin3

notes:
  5V
  GND
  gnd vcc sck sda

custom parts:
  ESP32-38PinWide: Generic 38-Pin ESP32 with wide format (only access to one side of pins on a breadboard) based on Stephen Lilley's HiLetgo ESP-WROOM-32 ESP32 ESP-32S Development Board.
